// Logisim project 2.2.circ as structural Verilog: 3 circuits, main circuit main
module main (
  input  in_1,
  input  in_2,
  output [1:0] out_3
);

  xor xor_1 (out_3[0], in_1, in_2);
  and and_1 (out_3[1], in_1, in_2);
endmodule

module add_4b (
  input  [3:0] in_1,
  input  in_2,
  input  [3:0] in_3,
  input  in_4,
  output [3:0] out_5,
  output [7:0] out_6,
  output retenu,
  output [7:0] out_8,
  output retenu_2
);

  wire add_1b_1_out_4, add_1b_2_out_4, add_1b_3_out_4;
  wire [7:0] adder_1_out, not_1_out, xor_1_out;

  Adder adder_1 (.a(8'h80), .b(8'h8c), .out(adder_1_out), .cout(retenu_2));  // open: cin
  add_1b add_1b_1 (.in_1({in_1[0], in_3[0]}), .Cin(in_2), .out_3(out_5[0]), .out_4(add_1b_1_out_4));
  add_1b add_1b_2 (.in_1({in_1[1], in_3[1]}), .Cin(add_1b_1_out_4), .out_3(out_5[1]), .out_4(add_1b_2_out_4));
  add_1b add_1b_3 (.in_1({in_1[2], in_3[2]}), .Cin(add_1b_2_out_4), .out_3(out_5[2]), .out_4(add_1b_3_out_4));
  add_1b add_1b_4 (.in_1({in_1[3], in_3[3]}), .Cin(add_1b_3_out_4), .out_3(out_5[3]));  // open: out_4
  assign xor_1_out = 8'h1 ^ not_1_out;  // XOR_Gate xor_1, 8 bits wide
  assign not_1_out = ~adder_1_out;  // NOT_Gate not_1, 8 bits wide
  Adder adder_2 (.a(8'h80), .b(8'h8c), .out(out_6), .cout(retenu));  // open: cin
  Multiplexer #(.width(8)) multiplexer_1 (.in0(adder_1_out), .in1(xor_1_out), .out(out_8), .sel(in_4));  // open: en
endmodule

module add_1b (
  input  [1:0] in_1,
  input  Cin,
  output out_3,
  output out_4
);

  wire and_1_out, and_2_out, xor_1_out;

  xor xor_1 (xor_1_out, in_1[0], in_1[1]);
  and and_1 (and_1_out, xor_1_out, Cin);
  and and_2 (and_2_out, in_1[0], in_1[1]);
  xor xor_2 (out_3, xor_1_out, Cin);
  or or_1 (out_4, and_1_out, and_2_out);
endmodule
