// Logisim project Instance de circuit + demi additionneur + additionneur complet +Additionneur 4 bits .circ as structural Verilog: 7 circuits, main circuit main
module main (
  input  in_1,
  input  in_2,
  output out_3,
  output out_4
);

  DA da_1 (.out_3(out_3), .in_1(in_1), .in_2(in_2), .out_4(out_4));
endmodule

module DA (
  input  in_1,
  input  in_2,
  output out_3,
  output out_4
);

  and and_1 (out_3, in_1, in_2);
  xor xor_1 (out_4, in_1, in_2);
endmodule

module mux21 (
  input  in_1,
  input  in_2,
  input  in_3,
  output out_4
);

  Multiplexer #(.disabled(0), .enable("false")) multiplexer_1 (.in0(in_1), .in1(in_2), .out(out_4), .sel(in_3));
endmodule

module AC (
  input  in_1,
  input  in_2,
  input  in_3,
  output out_4,
  output out_5
);

  wire da_1_out_3, da_1_out_4, da_2_out_3;

  or or_1 (out_4, da_1_out_3, da_2_out_3);
  DA da_1 (.out_3(da_1_out_3), .in_1(in_1), .in_2(in_2), .out_4(da_1_out_4));
  DA da_2 (.out_3(da_2_out_3), .in_1(da_1_out_4), .in_2(in_3), .out_4(out_5));
endmodule

module add4 (
  input  [3:0] in_1,
  input  [3:0] in_2,
  input  in_3,
  output out_4,
  output [3:0] out_5
);

  wire ac_1_out_4, ac_3_out_4, ac_4_out_4;

  AC ac_1 (.out_4(ac_1_out_4), .in_1(in_1[1]), .in_2(in_2[1]), .out_5(out_5[2]), .in_3(ac_3_out_4));
  AC ac_2 (.out_4(out_4), .in_1(in_1[0]), .in_2(in_2[0]), .out_5(out_5[3]), .in_3(ac_1_out_4));
  AC ac_3 (.out_4(ac_3_out_4), .in_1(in_1[2]), .in_2(in_2[2]), .out_5(out_5[1]), .in_3(ac_4_out_4));
  AC ac_4 (.out_4(ac_4_out_4), .in_1(in_1[3]), .in_2(in_2[3]), .out_5(out_5[0]), .in_3(in_3));
endmodule

module \Dé_éléctronique  (
  input  [2:0] in_1
);

  wire transcoder_1_a, transcoder_1_b, transcoder_1_c, transcoder_1_d, transcoder_1_e, transcoder_1_f,
       transcoder_1_g;

  transcoder transcoder_1 (
    .x(in_1[0]), .y(in_1[1]), .z(in_1[2]), .a(transcoder_1_a), .b(transcoder_1_b), .c(transcoder_1_c),
    .d(transcoder_1_d), .e(transcoder_1_e), .f(transcoder_1_f), .g(transcoder_1_g));
  LED led_1 (.in(transcoder_1_a));
  LED led_2 (.in(transcoder_1_c));
  LED led_3 (.in(transcoder_1_d));
  LED led_4 (.in(transcoder_1_f));
  LED led_5 (.in(transcoder_1_b));
  LED led_6 (.in(transcoder_1_e));
  LED led_7 (.in(transcoder_1_g));
endmodule

module transcoder (
  input  x,
  input  y,
  input  z,
  output a,
  output b,
  output c,
  output d,
  output e,
  output f,
  output g
);

  wire and_1_out, and_2_out, and_3_out, and_4_out, and_5_out, and_7_out, and_8_out, and_10_out, and_11_out,
       and_12_out, and_13_out, and_14_out, not_1_out, not_2_out, not_3_out, not_4_out, not_5_out, not_6_out,
       not_7_out, not_8_out, not_9_out, not_10_out, not_11_out, not_12_out, not_13_out, not_14_out;

  not not_1 (not_1_out, y);
  not not_2 (not_2_out, z);
  not not_3 (not_3_out, x);
  not not_4 (not_4_out, y);
  not not_5 (not_5_out, z);
  not not_6 (not_6_out, z);
  not not_7 (not_7_out, x);
  not not_8 (not_8_out, y);
  not not_9 (not_9_out, z);
  not not_10 (not_10_out, x);
  not not_11 (not_11_out, y);
  not not_12 (not_12_out, z);
  not not_13 (not_13_out, y);
  not not_14 (not_14_out, z);
  and and_1 (and_1_out, x, not_1_out);
  and and_2 (and_2_out, x, not_2_out);
  and and_3 (and_3_out, not_3_out, y);
  and and_4 (and_4_out, x, not_4_out);
  and and_5 (and_5_out, x, not_5_out);
  and and_6 (c, x, y, not_6_out);
  and and_7 (and_7_out, not_7_out, z);
  and and_8 (and_8_out, not_8_out, z);
  and and_9 (e, x, y, not_9_out);
  and and_10 (and_10_out, not_10_out, y);
  and and_11 (and_11_out, x, not_11_out);
  and and_12 (and_12_out, x, not_12_out);
  and and_13 (and_13_out, x, not_13_out);
  and and_14 (and_14_out, x, not_14_out);
  or or_1 (a, and_1_out, and_2_out);
  or or_2 (b, and_3_out, and_4_out, and_5_out);
  or or_3 (d, and_7_out, and_8_out);
  or or_4 (f, and_10_out, and_11_out, and_12_out);
  or or_5 (g, and_13_out, and_14_out);
endmodule
