// Logisim project TP 1 PArtie 1.circ as structural Verilog: 1 circuit, main circuit main
module main (
  input  in_1,
  input  in_2,
  input  in_3,
  input  [2:0] in_4,
  input  in_5,
  input  in_6,
  input  in_7,
  input  in_8,
  input  in_9,
  input  in_10,
  input  in_11,
  input  in_12,
  input  in_13,
  input  in_14,
  input  in_15,
  output [7:0] out_16
);

  wire and_1_out, and_2_out, and_3_out, and_4_out, and_5_out, and_6_out, and_7_out, and_8_out,
       multiplexer_1_out, not_1_out, not_2_out, not_3_out, or_1_out, or_2_out, or_3_out;

  not not_1 (not_1_out, in_13);
  not not_2 (not_2_out, in_14);
  not not_3 (not_3_out, in_15);
  and and_1 (and_1_out, in_13, in_14, in_15);
  and and_2 (and_2_out, in_13, in_14, not_3_out);
  and and_3 (and_3_out, in_13, not_2_out, in_15);
  and and_4 (and_4_out, in_13, not_2_out, not_3_out);
  and and_5 (and_5_out, not_1_out, in_14, in_15);
  and and_6 (and_6_out, not_1_out, in_14, in_15);
  and and_7 (and_7_out, not_1_out, not_2_out, in_15);
  and and_8 (and_8_out, not_1_out, not_2_out, not_3_out);
  LED led_1 (.in(and_1_out));
  LED led_2 (.in(and_2_out));
  LED led_3 (.in(and_3_out));
  LED led_4 (.in(and_4_out));
  LED led_5 (.in(and_5_out));
  LED led_6 (.in(and_6_out));
  LED led_7 (.in(and_7_out));
  LED led_8 (.in(and_8_out));
  Decoder #(.select(3)) decoder_1 (
    .out0(out_16[0]), .out1(out_16[1]), .out2(out_16[2]), .out3(out_16[3]), .out4(out_16[4]),
    .out5(out_16[5]), .out6(out_16[6]), .out7(out_16[7]), .sel(in_4));  // open: en
  Multiplexer multiplexer_1 (.in0(in_1), .in1(in_2), .out(multiplexer_1_out), .sel(in_3));  // open: en
  LED led_9 (.in(multiplexer_1_out));
  or or_1 (or_1_out, in_6, in_8, in_10, in_12);
  LED led_10 (.in(or_1_out));
  LED led_11 (.in(or_2_out));
  or or_2 (or_2_out, in_7, in_8, in_11, in_12);
  or or_3 (or_3_out, in_9, in_9, in_11, in_12);
  LED led_12 (.in(or_3_out));
endmodule
