// Logisim project TP 2 exo 2.circ as structural Verilog: 1 circuit, main circuit main
module main (
  input  [15:0] RES,
  output [2:0] NZP
);

  wire not_1_out, or_1_out, or_2_out;

  or or_1 (or_1_out, RES[14], RES[13], RES[12], RES[11], RES[10], RES[9], RES[8], RES[7], RES[6], RES[5], RES[4], RES[3], RES[2], RES[1], RES[0]);
  or or_2 (or_2_out, or_1_out, RES[15]);
  not not_1 (not_1_out, RES[15]);
  not not_2 (NZP[1], or_2_out);
  and and_1 (NZP[0], not_1_out, or_1_out);

  assign NZP[2] = RES[15];
endmodule
