// Logisim project multiplexeur détaillé.circ as structural Verilog: 1 circuit, main circuit main
module main (
  input  e0,
  input  c1,
  input  c2,
  input  e1,
  input  e2,
  input  e3,
  output S
);

  wire and_1_out, and_2_out, and_3_out, and_4_out, not_1_out, not_2_out;

  not not_1 (not_1_out, c1);
  not not_2 (not_2_out, c2);
  and and_1 (and_1_out, e0, not_1_out, not_2_out);
  and and_2 (and_2_out, not_1_out, e1, c2);
  and and_3 (and_3_out, c1, e2, not_2_out);
  and and_4 (and_4_out, c1, e3, c2);
  or or_1 (S, and_1_out, and_2_out, and_3_out, and_4_out);
endmodule
