// Logisim project tp3.circ as structural Verilog: 1 circuit, main circuit main
module main (
  input  [3:0] in_1,
  input  Clear,
  input  [3:0] in_3,
  output out_4,
  output out_5,
  output [3:0] out_6,
  output [7:0] out_7,
  output out_8,
  output out_9,
  output out_10
);

  wire button_1_out, button_2_out, clock_1_out, clock_2_out, clock_3_out, clock_4_out, clock_5_out,
       clock_6_out, clock_7_out, d_ff_1_qn, d_ff_2_q, d_ff_3_q, d_ff_4_q, d_ff_5_q, d_ff_6_q, d_ff_7_q,
       d_ff_8_q, d_ff_9_q, d_ff_10_q, d_ff_11_q, d_ff_12_q, d_ff_13_q, d_ff_14_q, not_1_out, not_2_out,
       not_3_out, not_4_out;
  wire [2:0] counter_1_q, counter_2_q, not_5_out;
  wire [3:0] register_1_q;

  Clock clock_1 (.out(clock_1_out));
  Clock clock_2 (.out(clock_2_out));
  Clock clock_3 (.out(clock_3_out));
  Clock clock_4 (.out(clock_4_out));
  Button button_1 (.out(button_1_out));
  D_Flip_Flop d_ff_1 (.clk(clock_1_out), .D(d_ff_1_qn), .Q(out_4), .Qn(d_ff_1_qn));  // open: preset, en, reset
  Clock clock_5 (.out(clock_5_out));
  Register #(.width(4)) register_1 (.D(out_6), .Q(register_1_q), .clk(clock_2_out), .clr(Clear));  // open: en
  not not_1 (not_1_out, button_2_out);
  Button button_2 (.out(button_2_out));
  Counter #(.width(3), .max('h7)) counter_1 (
    .Q(counter_1_q), .clk(clock_4_out), .clr(button_1_out));  // open: load, D, count, carry
  D_Flip_Flop d_ff_2 (.clk(clock_5_out), .D(d_ff_4_q), .Q(d_ff_2_q));  // open: Qn, preset, en, reset
  Adder #(.width(4)) adder_1 (.a(register_1_q), .b(in_3), .out(out_6));  // open: cin, cout
  D_Flip_Flop d_ff_3 (.clk(clock_3_out), .D(not_1_out), .Q(d_ff_3_q), .reset(button_2_out));  // open: Qn, preset, en
  D_Flip_Flop d_ff_4 (.clk(clock_5_out), .D(d_ff_2_q), .Q(d_ff_4_q), .Qn(out_5));  // open: preset, en, reset
  D_Flip_Flop d_ff_5 (.clk(clock_3_out), .D(d_ff_3_q), .Q(d_ff_5_q), .reset(button_2_out));  // open: Qn, preset, en
  D_Flip_Flop d_ff_6 (.clk(clock_3_out), .D(d_ff_5_q), .Q(d_ff_6_q), .reset(button_2_out));  // open: Qn, preset, en
  not not_2 (not_2_out, counter_1_q[0]);
  not not_3 (not_3_out, counter_1_q[1]);
  Clock clock_6 (.out(clock_6_out));
  not not_4 (not_4_out, counter_1_q[2]);
  D_Flip_Flop d_ff_7 (.clk(clock_6_out), .D(d_ff_14_q), .Q(d_ff_7_q));  // open: Qn, preset, en, reset
  RAM #(.addrWidth(4)) ram_1 (.addr(in_1), .data(out_7));  // open: sel, clk, ld, clr
  and and_1 (out_9, d_ff_3_q, d_ff_6_q, d_ff_5_q);
  D_Flip_Flop d_ff_8 (.clk(counter_1_q[0]), .Q(d_ff_8_q), .reset(not_2_out));  // open: D, Qn, preset, en
  D_Flip_Flop d_ff_9 (.clk(counter_1_q[1]), .D(d_ff_8_q), .Q(d_ff_9_q), .reset(not_3_out));  // open: Qn, preset, en
  D_Flip_Flop d_ff_10 (.clk(clock_6_out), .D(d_ff_11_q), .Q(d_ff_10_q));  // open: Qn, preset, en, reset
  D_Flip_Flop d_ff_11 (.clk(clock_6_out), .D(d_ff_7_q), .Q(d_ff_11_q));  // open: Qn, preset, en, reset
  Counter #(.width(3), .max('h7)) counter_2 (.Q(counter_2_q), .clk(clock_7_out));  // open: load, D, count, carry, clr
  Clock clock_7 (.out(clock_7_out));
  D_Flip_Flop d_ff_12 (.clk(counter_1_q[2]), .D(d_ff_9_q), .Q(d_ff_12_q), .reset(not_4_out));  // open: Qn, preset, en
  D_Flip_Flop d_ff_13 (.clk(clock_6_out), .D(d_ff_10_q), .Q(d_ff_13_q));  // open: Qn, preset, en, reset
  assign not_5_out = ~counter_2_q;  // NOT_Gate not_5, 3 bits wide
  and and_2 (out_10, d_ff_8_q, d_ff_12_q, d_ff_9_q);
  D_Flip_Flop d_ff_14 (.clk(clock_6_out), .D(d_ff_13_q), .Q(d_ff_14_q));  // open: Qn, preset, en, reset
  and and_3 (out_8, not_5_out[0], not_5_out[1], not_5_out[2]);
endmodule
